// Logisim project control-logic.circ as structural Verilog: 1 circuit, main circuit control_logic
module control_logic (
  input  [31:0] inst,
  input  BrEq,
  input  BrLt,
  output PCSel,
  output RegWEn,
  output [2:0] ImmSel,
  output BrUn,
  output ASel,
  output BSel,
  output [3:0] ALUSel,
  output MemRW,
  output [1:0] WBSel,
  output CSRSel,
  output CSRWen,
  output [5:0] out_15
);

  wire and_1_out, and_2_out, and_3_out, and_4_out, and_5_out, and_6_out, and_7_out, and_8_out, and_9_out,
       and_10_out, and_11_out, and_12_out, and_13_out, and_14_out, and_15_out, and_16_out, and_17_out,
       and_18_out, and_19_out, and_20_out, and_21_out, and_22_out, and_23_out, and_24_out, and_25_out,
       and_26_out, and_27_out, and_28_out, and_29_out, and_30_out, and_31_out, and_32_out, and_33_out,
       and_34_out, and_35_out, and_36_out, and_37_out, and_38_out, and_39_out, and_40_out, comparator_14_eq,
       comparator_15_eq, comparator_16_eq, comparator_17_eq, comparator_18_eq, comparator_19_eq,
       comparator_20_eq, comparator_21_eq, comparator_22_eq, comparator_23_eq, comparator_24_eq,
       comparator_25_eq, comparator_26_eq, comparator_27_eq, comparator_28_eq, comparator_29_eq,
       comparator_30_eq, comparator_31_eq, comparator_32_eq, comparator_33_eq, comparator_34_eq,
       comparator_35_eq, comparator_36_eq, comparator_37_eq, comparator_38_eq, comparator_39_eq,
       comparator_40_eq, comparator_41_eq, comparator_42_eq, comparator_43_gt, comparator_44_lt,
       comparator_45_eq, comparator_46_eq, f00, f01, f20, multiplexer_2_out, not_1_out, not_2_out, oc03,
       oc6f, oc13, oc17, oc23, oc33, oc37, oc63, oc67, oc73, or_1_out, or_3_out, priority_encoder_1_en_out,
       priority_encoder_2_en_out, priority_encoder_3_en_out;
  wire [2:0] bit_extender_4_out;
  wire [3:0] priority_encoder_1_out, priority_encoder_2_out, priority_encoder_3_out;
  wire [5:0] adder_1_out, adder_2_out, bit_extender_1_out, bit_extender_2_out, bit_extender_3_out,
       multiplexer_1_out, multiplexer_3_out, subtractor_1_out;

  Comparator #(.mode("unsigned"), .width(7)) comparator_1 (.a(inst[6:0]), .b(7'b0100011), .eq(oc23));  // open: gt, lt
  Comparator #(.mode("unsigned"), .width(7)) comparator_2 (.a(inst[6:0]), .b(7'b1100011), .eq(oc63));  // open: gt, lt
  Comparator #(.mode("unsigned"), .width(7)) comparator_3 (.a(inst[6:0]), .b(7'b0010111), .eq(oc17));  // open: gt, lt
  Comparator #(.mode("unsigned"), .width(7)) comparator_4 (.a(inst[6:0]), .b(7'b0110111), .eq(oc37));  // open: gt, lt
  Comparator #(.mode("unsigned"), .width(7)) comparator_5 (.a(inst[6:0]), .b(7'b1101111), .eq(oc6f));  // open: gt, lt
  Comparator #(.mode("unsigned"), .width(7)) comparator_6 (.a(inst[6:0]), .b(7'b1100111), .eq(oc67));  // open: gt, lt
  Comparator #(.mode("unsigned"), .width(7)) comparator_7 (.a(inst[6:0]), .b(7'b1110011), .eq(oc73));  // open: gt, lt
  Comparator #(.mode("unsigned"), .width(7)) comparator_8 (.a(inst[31:25]), .b({7{1'b0}}), .eq(f00));  // open: gt, lt
  Comparator #(.mode("unsigned"), .width(7)) comparator_9 (.a(inst[31:25]), .b(7'b0000001), .eq(f01));  // open: gt, lt
  Comparator #(.mode("unsigned"), .width(7)) comparator_10 (.a(inst[31:25]), .b(7'b0100000), .eq(f20));  // open: gt, lt
  Comparator #(.mode("unsigned"), .width(7)) comparator_11 (.a(inst[6:0]), .b(7'b0110011), .eq(oc33));  // open: gt, lt
  Comparator #(.mode("unsigned"), .width(7)) comparator_12 (.a(inst[6:0]), .b(7'b0000011), .eq(oc03));  // open: gt, lt
  Comparator #(.mode("unsigned"), .width(7)) comparator_13 (.a(inst[6:0]), .b(7'b0010011), .eq(oc13));  // open: gt, lt
  ROM #(.addrWidth(6), .dataWidth(16)) rom_1 (
    .addr(out_15), .data({RegWEn, ImmSel, BrUn, ASel, BSel, ALUSel, MemRW, WBSel, CSRSel, CSRWen}));
  Comparator #(.mode("unsigned"), .width(3)) comparator_14 (
    .a(inst[14:12]), .b(3'b000), .eq(comparator_14_eq));  // open: gt, lt
  Comparator #(.mode("unsigned"), .width(3)) comparator_15 (
    .a(inst[14:12]), .b(3'b001), .eq(comparator_15_eq));  // open: gt, lt
  Comparator #(.mode("unsigned"), .width(3)) comparator_16 (
    .a(inst[14:12]), .b(3'b010), .eq(comparator_16_eq));  // open: gt, lt
  Comparator #(.mode("unsigned"), .width(3)) comparator_17 (
    .a(inst[14:12]), .b(3'b011), .eq(comparator_17_eq));  // open: gt, lt
  Comparator #(.mode("unsigned"), .width(3)) comparator_18 (
    .a(inst[14:12]), .b(3'b100), .eq(comparator_18_eq));  // open: gt, lt
  Comparator #(.mode("unsigned"), .width(3)) comparator_19 (
    .a(inst[14:12]), .b(3'b101), .eq(comparator_19_eq));  // open: gt, lt
  Comparator #(.mode("unsigned"), .width(3)) comparator_20 (
    .a(inst[14:12]), .b(3'b110), .eq(comparator_20_eq));  // open: gt, lt
  Comparator #(.mode("unsigned"), .width(3)) comparator_21 (
    .a(inst[14:12]), .b(3'b111), .eq(comparator_21_eq));  // open: gt, lt
  Comparator #(.mode("unsigned"), .width(3)) comparator_22 (
    .a(inst[14:12]), .b(3'b000), .eq(comparator_22_eq));  // open: gt, lt
  Comparator #(.mode("unsigned"), .width(3)) comparator_23 (
    .a(inst[14:12]), .b(3'b001), .eq(comparator_23_eq));  // open: gt, lt
  Comparator #(.mode("unsigned"), .width(3)) comparator_24 (
    .a(inst[14:12]), .b(3'b010), .eq(comparator_24_eq));  // open: gt, lt
  Comparator #(.mode("unsigned"), .width(3)) comparator_25 (
    .a(inst[14:12]), .b(3'b000), .eq(comparator_25_eq));  // open: gt, lt
  Comparator #(.mode("unsigned"), .width(3)) comparator_26 (
    .a(inst[14:12]), .b(3'b001), .eq(comparator_26_eq));  // open: gt, lt
  Comparator #(.mode("unsigned"), .width(3)) comparator_27 (
    .a(inst[14:12]), .b(3'b010), .eq(comparator_27_eq));  // open: gt, lt
  Comparator #(.mode("unsigned"), .width(3)) comparator_28 (
    .a(inst[14:12]), .b(3'b100), .eq(comparator_28_eq));  // open: gt, lt
  Comparator #(.mode("unsigned"), .width(3)) comparator_29 (
    .a(inst[14:12]), .b(3'b101), .eq(comparator_29_eq));  // open: gt, lt
  Comparator #(.mode("unsigned"), .width(3)) comparator_30 (
    .a(inst[14:12]), .b(3'b110), .eq(comparator_30_eq));  // open: gt, lt
  Comparator #(.mode("unsigned"), .width(3)) comparator_31 (
    .a(inst[14:12]), .b(3'b111), .eq(comparator_31_eq));  // open: gt, lt
  Comparator #(.mode("unsigned"), .width(3)) comparator_32 (
    .a(inst[14:12]), .b(3'b000), .eq(comparator_32_eq));  // open: gt, lt
  Comparator #(.mode("unsigned"), .width(3)) comparator_33 (
    .a(inst[14:12]), .b(3'b001), .eq(comparator_33_eq));  // open: gt, lt
  Comparator #(.mode("unsigned"), .width(3)) comparator_34 (
    .a(inst[14:12]), .b(3'b010), .eq(comparator_34_eq));  // open: gt, lt
  Comparator #(.mode("unsigned"), .width(3)) comparator_35 (
    .a(inst[14:12]), .b(3'b000), .eq(comparator_35_eq));  // open: gt, lt
  Comparator #(.mode("unsigned"), .width(3)) comparator_36 (
    .a(inst[14:12]), .b(3'b001), .eq(comparator_36_eq));  // open: gt, lt
  Comparator #(.mode("unsigned"), .width(3)) comparator_37 (
    .a(inst[14:12]), .b(3'b100), .eq(comparator_37_eq));  // open: gt, lt
  Comparator #(.mode("unsigned"), .width(3)) comparator_38 (
    .a(inst[14:12]), .b(3'b101), .eq(comparator_38_eq));  // open: gt, lt
  Comparator #(.mode("unsigned"), .width(3)) comparator_39 (
    .a(inst[14:12]), .b(3'b110), .eq(comparator_39_eq));  // open: gt, lt
  Comparator #(.mode("unsigned"), .width(3)) comparator_40 (
    .a(inst[14:12]), .b(3'b111), .eq(comparator_40_eq));  // open: gt, lt
  Comparator #(.mode("unsigned"), .width(3)) comparator_41 (
    .a(inst[14:12]), .b(3'b001), .eq(comparator_41_eq));  // open: gt, lt
  Comparator #(.mode("unsigned"), .width(3)) comparator_42 (
    .a(inst[14:12]), .b(3'b101), .eq(comparator_42_eq));  // open: gt, lt
  and and_1 (and_1_out, comparator_14_eq, oc33);
  and and_2 (and_2_out, comparator_15_eq, oc33);
  and and_3 (and_3_out, comparator_16_eq, oc33);
  and and_4 (and_4_out, comparator_17_eq, oc33);
  and and_5 (and_5_out, comparator_18_eq, oc33);
  and and_6 (and_6_out, comparator_19_eq, oc33);
  and and_7 (and_7_out, comparator_20_eq, oc33);
  and and_8 (and_8_out, comparator_21_eq, oc33);
  and and_9 (and_9_out, comparator_22_eq, oc03);
  and and_10 (and_10_out, comparator_23_eq, oc03);
  and and_11 (and_11_out, comparator_24_eq, oc03);
  and and_12 (and_12_out, comparator_25_eq, oc13);
  and and_13 (and_13_out, comparator_26_eq, oc13);
  and and_14 (and_14_out, comparator_27_eq, oc13);
  and and_15 (and_15_out, comparator_28_eq, oc13);
  and and_16 (and_16_out, comparator_29_eq, oc13);
  and and_17 (and_17_out, comparator_30_eq, oc13);
  and and_18 (and_18_out, comparator_31_eq, oc13);
  and and_19 (and_19_out, comparator_32_eq, oc23);
  and and_20 (and_20_out, comparator_33_eq, oc23);
  and and_21 (and_21_out, comparator_34_eq, oc23);
  and and_22 (and_22_out, comparator_35_eq, oc63);
  and and_23 (and_23_out, comparator_36_eq, oc63);
  and and_24 (and_24_out, comparator_37_eq, oc63);
  and and_25 (and_25_out, comparator_38_eq, oc63);
  and and_26 (and_26_out, comparator_39_eq, oc63);
  and and_27 (and_27_out, comparator_40_eq, oc63);
  and and_28 (and_28_out, comparator_41_eq, oc73);
  and and_29 (and_29_out, comparator_42_eq, oc73);
  and and_30 (and_30_out, f00, and_1_out);
  and and_31 (and_31_out, f01, and_1_out);
  and and_32 (and_32_out, f20, and_1_out);
  and and_33 (and_33_out, and_2_out, f00);
  and and_34 (and_34_out, and_2_out, f01);
  and and_35 (and_35_out, f00, and_6_out);
  and and_36 (and_36_out, f20, and_6_out);
  and and_37 (and_37_out, and_16_out, f00);
  and and_38 (and_38_out, and_16_out, f20);
  Priority_Encoder #(.select(4)) priority_encoder_1 (
    .in0(and_9_out), .in1(and_10_out), .in2(and_11_out), .in3(and_12_out), .in4(and_13_out),
    .in5(and_14_out), .in6(and_15_out), .in7(and_37_out), .in8(and_38_out), .in9(and_17_out),
    .in10(and_18_out), .in11(and_19_out), .in12(and_20_out), .in13(and_21_out), .out(priority_encoder_1_out),
    .en_out(priority_encoder_1_en_out));  // open: in14, in15, gs, en_in
  Priority_Encoder #(.select(4)) priority_encoder_2 (
    .in0(and_30_out), .in1(and_31_out), .in2(and_32_out), .in3(and_33_out), .in4(and_34_out),
    .in5(and_4_out), .in6(and_3_out), .in7(and_5_out), .in8(and_35_out), .in9(and_36_out), .in10(and_7_out),
    .in11(and_8_out), .out(priority_encoder_2_out), .en_out(priority_encoder_2_en_out));  // open: in12, in13, in14, in15, gs, en_in
  assign bit_extender_1_out = {{2{1'b0}}, priority_encoder_1_out};  // Bit_Extender bit_extender_1
  Priority_Encoder #(.select(4)) priority_encoder_3 (
    .in0(and_22_out), .in1(and_23_out), .in2(and_24_out), .in3(and_25_out), .in4(and_26_out),
    .in5(and_27_out), .in6(oc17), .in7(oc37), .in8(oc6f), .in9(oc67), .in10(and_28_out), .in11(and_29_out),
    .out(priority_encoder_3_out), .en_out(priority_encoder_3_en_out));  // open: in12, in13, in14, in15, gs, en_in
  assign bit_extender_2_out = {{2{1'b0}}, priority_encoder_2_out};  // Bit_Extender bit_extender_2
  Adder #(.width(6)) adder_1 (.a(bit_extender_1_out), .b(6'b001100), .out(adder_1_out));  // open: cin, cout
  assign bit_extender_3_out = {{2{1'b0}}, priority_encoder_3_out};  // Bit_Extender bit_extender_3
  not not_1 (not_1_out, BrEq);
  not not_2 (not_2_out, BrLt);
  or or_1 (or_1_out, not_2_out, BrEq);
  Comparator #(.mode("unsigned"), .width(6)) comparator_43 (
    .a(out_15), .b(6'b011001), .gt(comparator_43_gt));  // open: eq, lt
  Comparator #(.mode("unsigned"), .width(6)) comparator_44 (
    .a(out_15), .b(6'b100000), .lt(comparator_44_lt));  // open: gt, eq
  Multiplexer #(.enable("false"), .width(6)) multiplexer_1 (
    .in0(adder_1_out), .in1(6'b001111), .out(multiplexer_1_out), .sel(priority_encoder_1_en_out));
  Adder #(.width(6)) adder_2 (.a(bit_extender_3_out), .b(6'b011010), .out(adder_2_out));  // open: cin, cout
  Multiplexer #(.enable("false"), .select(3)) multiplexer_2 (
    .in0(BrEq), .in1(not_1_out), .in2(BrLt), .in3(or_1_out), .in4(BrLt), .in5(or_1_out),
    .out(multiplexer_2_out), .sel(bit_extender_4_out));  // open: in6, in7
  Bit_Extender #(.in_width(6), .out_width(3)) bit_extender_4 (.in(subtractor_1_out), .out(bit_extender_4_out));
  Subtractor #(.width(6)) subtractor_1 (.a(out_15), .b(6'b011010), .out(subtractor_1_out));  // open: bin, bout
  and and_39 (and_39_out, comparator_43_gt, comparator_44_lt);
  and and_40 (and_40_out, multiplexer_2_out, and_39_out);
  Multiplexer #(.enable("false"), .width(6)) multiplexer_3 (
    .in0(bit_extender_2_out), .in1(multiplexer_1_out), .out(multiplexer_3_out),
    .sel(priority_encoder_2_en_out));
  Multiplexer #(.enable("false"), .width(6)) multiplexer_4 (
    .in0(adder_2_out), .in1(multiplexer_3_out), .out(out_15), .sel(priority_encoder_3_en_out));
  or or_2 (PCSel, and_40_out, or_3_out);
  Comparator #(.mode("unsigned"), .width(6)) comparator_45 (
    .a(out_15), .b(6'b100010), .eq(comparator_45_eq));  // open: gt, lt
  Comparator #(.mode("unsigned"), .width(6)) comparator_46 (
    .a(out_15), .b(6'b100011), .eq(comparator_46_eq));  // open: gt, lt
  or or_3 (or_3_out, comparator_45_eq, comparator_46_eq);

  // Other names for the same wires on the sheet: opcode[6:0] = inst[6:0]; funct3[2:0] = inst[14:12];
  //   funct7[6:0] = inst[31:25]; ROMInput[5:0] = out_15

  // Notes on the sheet:
  //   INPUTS to your circuit
  //   contents of rom_1 (hex, n*v repeats v):
  //   8004 8104 8184 8024 8124 8164 8044 8084 80a4 81a4 80c4 80e4 9200 9200 9200 9204 9224 9244 9284 92a4
  //   93a4 92c4 92e4 2214 2214 2214 4*3604 3e04 3e04 c604 c3e4 d60c 920c 71e7 73e5
  //   ROM FOR CONTROL LOGIC
  //   DON'T CHANGE THE LOCATIONS OF THE INPUTS AND OUTPUTS!
  //   OUTPUT from your circuit
  //   Reminder: Use combinational logic for PCSel
endmodule
