// Logisim project cpu.circ as structural Verilog: 1 circuit, main circuit cpu
module cpu (
  input  clk,
  input  [31:0] INSTRUCTION,
  input  [31:0] MEM_READ_DATA,
  output [31:0] MEM_WRITE_ADDRESS,
  output [31:0] PROGRAM_COUNTER,
  output [31:0] ra,
  output [31:0] sp,
  output [31:0] t0,
  output [31:0] t1,
  output [31:0] t2,
  output [31:0] s0,
  output [31:0] s1,
  output [31:0] a0,
  output [31:0] tohost,
  output [3:0] MEM_WRITE_ENABLE,
  output [31:0] MEM_WRITE_DATA
);

  wire ASel, BrEq, BrLt, BrUn, BSel, CSRSel, CSRWen, FirstInst, MemRW, PCSel, register_1_q, RegWEn;
  wire [1:0] WBSel;
  wire [2:0] ImmSel;
  wire [3:0] ALUSel, multiplexer_8_out, multiplexer_9_out, multiplexer_12_out;
  wire [31:0] adder_1_out, bit_extender_1_out, bit_extender_2_out, bit_extender_3_out, bit_extender_4_out,
       bit_extender_5_out, bit_extender_6_out, bit_extender_7_out, bit_extender_8_out, Data1, Data2,
       Immediate, INSPIPELINE, INSPIPELINE_q, multiplexer_1_out, multiplexer_2_out, multiplexer_4_out,
       multiplexer_5_out, multiplexer_6_out, multiplexer_7_out, multiplexer_10_out, multiplexer_11_out,
       PCPIPELINE, PCplus4, shifter_1_out, shifter_2_out, shifter_3_out, shifter_4_out, WriteData;

  Adder #(.width(32)) adder_1 (.a(PROGRAM_COUNTER), .b(32'h4), .out(adder_1_out));  // open: cin, cout
  Register #(.width(1)) register_1 (.D(1'b1), .clk(clk), .Q(register_1_q));  // open: en, clr
  Multiplexer #(.enable("false"), .width(32)) multiplexer_1 (
    .in0(adder_1_out), .in1(MEM_WRITE_ADDRESS), .out(multiplexer_1_out), .sel(PCSel));
  Multiplexer #(.enable("false"), .width(32)) multiplexer_2 (
    .in0(INSTRUCTION), .in1(32'h13), .out(multiplexer_2_out), .sel(PCSel));
  not not_1 (FirstInst, register_1_q);
  Register #(.width(32)) PC (.D(multiplexer_1_out), .clk(clk), .Q(PROGRAM_COUNTER));  // open: en, clr
  Register #(.width(32)) u_INSPIPELINE (.D(multiplexer_2_out), .clk(clk), .Q(INSPIPELINE_q));  // open: en, clr
  Register #(.width(32)) u_PCPIPELINE (.D(PROGRAM_COUNTER), .clk(clk), .Q(PCPIPELINE));  // open: en, clr
  Multiplexer #(.enable("false"), .width(32)) multiplexer_3 (
    .in0(INSPIPELINE_q), .in1(32'h13), .out(INSPIPELINE), .sel(FirstInst));
  Adder #(.width(32)) adder_2 (.a(32'h4), .b(PCPIPELINE), .out(PCplus4));  // open: cin, cout
  control_logic control_logic_1 (
    .CSRWen(CSRWen), .PCSel(PCSel), .RegWEn(RegWEn), .ImmSel(ImmSel), .BrUn(BrUn), .ASel(ASel), .BSel(BSel),
    .ALUSel(ALUSel), .MemRW(MemRW), .WBSel(WBSel), .CSRSel(CSRSel), .inst(INSPIPELINE), .BrEq(BrEq),
    .BrLt(BrLt));  // open: out_15
  Multiplexer #(.enable("false"), .select(2), .width(32)) multiplexer_4 (
    .in0(WriteData), .in1(MEM_WRITE_ADDRESS), .in3(PCplus4), .out(multiplexer_4_out), .sel(WBSel));  // open: in2
  branch_comp branch_comp_1 (.rs1(Data1), .rs2(Data2), .BrUn(BrUn), .BrEq(BrEq), .BrLt(BrLt));
  imm_gen imm_gen_1 (.inst(INSPIPELINE), .ImmSel(ImmSel), .imm(Immediate));
  regfile regfile_1 (
    .rs1(INSPIPELINE[19:15]), .rs2(INSPIPELINE[24:20]), .rd(INSPIPELINE[11:7]),
    .Write_Data(multiplexer_4_out), .RegWEn(RegWEn), .clk(clk), .ra(ra), .sp(sp), .t0(t0), .t1(t1), .t2(t2),
    .s0(s0), .s1(s1), .a0(a0), .Read_Data_1(Data1), .Read_Data_2(Data2));
  Multiplexer #(.enable("false"), .width(32)) multiplexer_5 (
    .in0(MEM_WRITE_ADDRESS), .in1(Data1), .out(multiplexer_5_out), .sel(CSRSel));
  Multiplexer #(.enable("false"), .width(32)) multiplexer_6 (
    .in0(Data1), .in1(PCPIPELINE), .out(multiplexer_6_out), .sel(ASel));
  Multiplexer #(.enable("false"), .width(32)) multiplexer_7 (
    .in0(Data2), .in1(Immediate), .out(multiplexer_7_out), .sel(BSel));
  // csr csr_1: pin names not known; wires that end beside it: INSPIPELINE[31:20], multiplexer_5_out, CSRWen, clk, tohost
  alu alu_1 (.Result(MEM_WRITE_ADDRESS), .A(multiplexer_6_out), .B(multiplexer_7_out), .ALUSel(ALUSel));
  Multiplexer #(.enable("false"), .select(2), .width(4)) multiplexer_8 (
    .in0(4'b0001), .in1(4'b0010), .in2(4'b0100), .in3(4'b1000), .out(multiplexer_8_out),
    .sel(MEM_WRITE_ADDRESS[1:0]));
  assign bit_extender_1_out = {{24{MEM_READ_DATA[7]}}, MEM_READ_DATA[7:0]};  // Bit_Extender bit_extender_1
  assign bit_extender_2_out = {{24{MEM_READ_DATA[15]}}, MEM_READ_DATA[15:8]};  // Bit_Extender bit_extender_2
  assign bit_extender_3_out = {{24{MEM_READ_DATA[23]}}, MEM_READ_DATA[23:16]};  // Bit_Extender bit_extender_3
  assign bit_extender_4_out = {{24{MEM_READ_DATA[31]}}, MEM_READ_DATA[31:24]};  // Bit_Extender bit_extender_4
  assign bit_extender_5_out = {{16{MEM_READ_DATA[15]}}, MEM_READ_DATA[15:0]};  // Bit_Extender bit_extender_5
  assign bit_extender_6_out = {{16{MEM_READ_DATA[31]}}, MEM_READ_DATA[31:16]};  // Bit_Extender bit_extender_6
  Multiplexer #(.enable("false"), .select(2), .width(4)) multiplexer_9 (
    .in0(4'b0011), .in2(4'b1100), .out(multiplexer_9_out), .sel(MEM_WRITE_ADDRESS[1:0]));  // open: in1, in3
  Multiplexer #(.enable("false"), .select(2), .width(32)) multiplexer_10 (
    .in0(bit_extender_1_out), .in1(bit_extender_2_out), .in2(bit_extender_3_out), .in3(bit_extender_4_out),
    .out(multiplexer_10_out), .sel(MEM_WRITE_ADDRESS[1:0]));
  Multiplexer #(.enable("false"), .select(2), .width(32)) multiplexer_11 (
    .in0(bit_extender_5_out), .in2(bit_extender_6_out), .out(multiplexer_11_out), .sel(MEM_WRITE_ADDRESS[1:0]));  // open: in1, in3
  Multiplexer #(.enable("false"), .select(2), .width(4)) multiplexer_12 (
    .in0(multiplexer_8_out), .in1(multiplexer_9_out), .in2(4'b1111), .out(multiplexer_12_out),
    .sel(INSPIPELINE[13:12]));  // open: in3
  Multiplexer #(.enable("false"), .select(2), .width(32)) multiplexer_13 (
    .in0(multiplexer_10_out), .in1(multiplexer_11_out), .in2(MEM_READ_DATA), .out(WriteData),
    .sel(INSPIPELINE[13:12]));  // open: in3
  Multiplexer #(.enable("false"), .width(4)) multiplexer_14 (
    .in0(4'b0000), .in1(multiplexer_12_out), .out(MEM_WRITE_ENABLE), .sel(MemRW));
  assign bit_extender_7_out = {{24{1'b0}}, Data2[7:0]};  // Bit_Extender bit_extender_7
  assign bit_extender_8_out = {{16{1'b0}}, Data2[15:0]};  // Bit_Extender bit_extender_8
  Shifter #(.width(32)) shifter_1 (.in(bit_extender_7_out), .\dist (5'b01000), .out(shifter_1_out));
  Shifter #(.width(32)) shifter_2 (.in(bit_extender_7_out), .\dist (5'b10000), .out(shifter_2_out));
  Shifter #(.width(32)) shifter_3 (.in(bit_extender_7_out), .\dist (5'b11000), .out(shifter_3_out));
  Shifter #(.width(32)) shifter_4 (.in(bit_extender_8_out), .\dist (5'b10000), .out(shifter_4_out));
  Multiplexer #(.enable("false"), .select(4), .width(32)) multiplexer_15 (
    .in0(MEM_READ_DATA), .in1(bit_extender_7_out), .in2(shifter_1_out), .in3(bit_extender_8_out),
    .in4(shifter_2_out), .in8(shifter_3_out), .in12(shifter_4_out), .in15(Data2), .out(MEM_WRITE_DATA),
    .sel(MEM_WRITE_ENABLE));  // open: in5, in6, in7, in9, in10, in11, in13, in14

  // Other names for the same wires on the sheet: rd[4:0] = INSPIPELINE[11:7]; rs1[4:0] = INSPIPELINE[19:15];
  //   rs2[4:0] = INSPIPELINE[24:20]; Final2Bits[1:0] = MEM_WRITE_ADDRESS[1:0]; Result[31:0] = MEM_WRITE_ADDRESS

  // Notes on the sheet:
  //   Output to IMEM
  //   IMEM (do **NOT** move this)
  //   Inputs from IMEM
  //   It is OK to move the PC, RegFile, ALU, MEM, Branch Comp, Imm Gen, and Control Logic to wherever is most convenient for you when constructing your CPU, and to delete this text
  //   Inputs/Outputs for testing. Do **NOT** move these.
  //   Outputs To DMEM
  //   DMEM (do **NOT** move this)
  //   Inputs From DMEM
endmodule
