// Logisim project imm-gen.circ as structural Verilog: 1 circuit, main circuit imm_gen
module imm_gen (
  input  [31:0] inst,
  input  [2:0] ImmSel,
  output [31:0] imm
);

  wire [11:0] bit_extender_4_out;
  wire [19:0] bit_extender_3_out;
  wire [26:0] bit_extender_2_out;
  wire [31:0] bit_extender_1_out, bit_extender_5_out;

  assign bit_extender_1_out = {{20{inst[31]}}, inst[31:20]};  // Bit_Extender bit_extender_1
  assign bit_extender_2_out = {{20{inst[31]}}, inst[31:25]};  // Bit_Extender bit_extender_2
  assign bit_extender_3_out = {{19{inst[31]}}, inst[31]};  // Bit_Extender bit_extender_3
  assign bit_extender_4_out = {{11{inst[31]}}, inst[31]};  // Bit_Extender bit_extender_4
  Multiplexer #(.enable("false"), .select(3), .width(32)) multiplexer_1 (
    .in0(inst), .in1(bit_extender_1_out), .in2({bit_extender_2_out, inst[11:7]}),
    .in3({bit_extender_3_out, inst[7], inst[30:25], inst[11:8], 1'b0}), .in4({inst[31:12], {12{1'b0}}}),
    .in5({bit_extender_4_out, inst[19:12], inst[20], inst[30:21], 1'b0}), .in6(inst),
    .in7(bit_extender_5_out), .out(imm), .sel(ImmSel));
  assign bit_extender_5_out = {{27{1'b0}}, inst[19:15]};  // Bit_Extender bit_extender_5

  // Notes on the sheet:
  //   INPUTS to your circuit
  //   DON'T CHANGE THE LOCATIONS OF THE INPUTS AND OUTPUTS!
  //   OUTPUT from your circuit
endmodule
