// Logisim project regfile.circ as structural Verilog: 1 circuit, main circuit regfile
module regfile (
  input  [4:0] rs1,
  input  [4:0] rs2,
  input  [4:0] rd,
  input  [31:0] Write_Data,
  input  RegWEn,
  input  clk,
  output [31:0] ra,
  output [31:0] sp,
  output [31:0] t0,
  output [31:0] t1,
  output [31:0] t2,
  output [31:0] s0,
  output [31:0] s1,
  output [31:0] a0,
  output [31:0] Read_Data_1,
  output [31:0] Read_Data_2
);

  wire comparator_1_eq, comparator_2_eq, comparator_3_eq, comparator_4_eq, comparator_5_eq, comparator_6_eq,
       comparator_7_eq, comparator_8_eq, comparator_9_eq, comparator_10_eq, comparator_11_eq,
       comparator_12_eq, comparator_13_eq, comparator_14_eq, comparator_15_eq, comparator_16_eq,
       comparator_17_eq, comparator_18_eq, comparator_19_eq, comparator_20_eq, comparator_21_eq,
       comparator_22_eq, comparator_23_eq, comparator_24_eq, comparator_25_eq, comparator_26_eq,
       comparator_27_eq, comparator_28_eq, comparator_29_eq, comparator_30_eq, comparator_31_eq;
  wire [31:0] R0Out, R1IN, R2IN, R3IN, R3Out, R4IN, R4Out, R5IN, R6IN, R7IN, R8IN, R9IN, R10IN, R11IN,
       R11Out, R12IN, R12Out, R13IN, R13Out, R14IN, R14Out, R15IN, R15Out, R16IN, R16Out, R17IN, R17Out,
       R18IN, R18Out, R19IN, R19Out, R20IN, R20Out, R21IN, R21Out, R22IN, R22Out, R23IN, R23Out, R24IN,
       R24Out, R25IN, R25Out, R26IN, R26Out, R27IN, R27Out, R28IN, R28Out, R29IN, R29Out, R30IN, R30Out,
       R31IN, R31Out;

  Register #(.width(32)) register_1 (.D(R0Out), .en(RegWEn), .clk(clk), .Q(R0Out));  // open: clr
  Register #(.width(32)) register_2 (.D(R8IN), .en(RegWEn), .clk(clk), .Q(s0));  // open: clr
  Register #(.width(32)) register_3 (.D(R16IN), .en(RegWEn), .clk(clk), .Q(R16Out));  // open: clr
  Register #(.width(32)) register_4 (.D(R24IN), .en(RegWEn), .clk(clk), .Q(R24Out));  // open: clr
  Register #(.width(32)) register_5 (.D(R1IN), .en(RegWEn), .clk(clk), .Q(ra));  // open: clr
  Register #(.width(32)) register_6 (.D(R9IN), .en(RegWEn), .clk(clk), .Q(s1));  // open: clr
  Register #(.width(32)) register_7 (.D(R17IN), .en(RegWEn), .clk(clk), .Q(R17Out));  // open: clr
  Register #(.width(32)) register_8 (.D(R25IN), .en(RegWEn), .clk(clk), .Q(R25Out));  // open: clr
  Register #(.width(32)) register_9 (.D(R2IN), .en(RegWEn), .clk(clk), .Q(sp));  // open: clr
  Register #(.width(32)) register_10 (.D(R10IN), .en(RegWEn), .clk(clk), .Q(a0));  // open: clr
  Register #(.width(32)) register_11 (.D(R18IN), .en(RegWEn), .clk(clk), .Q(R18Out));  // open: clr
  Register #(.width(32)) register_12 (.D(R26IN), .en(RegWEn), .clk(clk), .Q(R26Out));  // open: clr
  Multiplexer #(.enable("false"), .select(5), .width(32)) multiplexer_1 (
    .in0(R0Out), .in1(ra), .in2(sp), .in3(R3Out), .in4(R4Out), .in5(t0), .in6(t1), .in7(t2), .in8(s0),
    .in9(s1), .in10(a0), .in11(R11Out), .in12(R12Out), .in13(R13Out), .in14(R14Out), .in15(R15Out),
    .in16(R16Out), .in17(R17Out), .in18(R18Out), .in19(R19Out), .in20(R20Out), .in21(R21Out), .in22(R22Out),
    .in23(R23Out), .in24(R24Out), .in25(R25Out), .in26(R26Out), .in27(R27Out), .in28(R28Out), .in29(R29Out),
    .in30(R30Out), .in31(R31Out), .out(Read_Data_2), .sel(rs2));
  Register #(.width(32)) register_13 (.D(R3IN), .en(RegWEn), .clk(clk), .Q(R3Out));  // open: clr
  Register #(.width(32)) register_14 (.D(R11IN), .en(RegWEn), .clk(clk), .Q(R11Out));  // open: clr
  Register #(.width(32)) register_15 (.D(R19IN), .en(RegWEn), .clk(clk), .Q(R19Out));  // open: clr
  Register #(.width(32)) register_16 (.D(R27IN), .en(RegWEn), .clk(clk), .Q(R27Out));  // open: clr
  Register #(.width(32)) register_17 (.D(R4IN), .en(RegWEn), .clk(clk), .Q(R4Out));  // open: clr
  Register #(.width(32)) register_18 (.D(R12IN), .en(RegWEn), .clk(clk), .Q(R12Out));  // open: clr
  Register #(.width(32)) register_19 (.D(R20IN), .en(RegWEn), .clk(clk), .Q(R20Out));  // open: clr
  Register #(.width(32)) register_20 (.D(R28IN), .en(RegWEn), .clk(clk), .Q(R28Out));  // open: clr
  Register #(.width(32)) register_21 (.D(R5IN), .en(RegWEn), .clk(clk), .Q(t0));  // open: clr
  Register #(.width(32)) register_22 (.D(R13IN), .en(RegWEn), .clk(clk), .Q(R13Out));  // open: clr
  Register #(.width(32)) register_23 (.D(R21IN), .en(RegWEn), .clk(clk), .Q(R21Out));  // open: clr
  Register #(.width(32)) register_24 (.D(R29IN), .en(RegWEn), .clk(clk), .Q(R29Out));  // open: clr
  Register #(.width(32)) register_25 (.D(R6IN), .en(RegWEn), .clk(clk), .Q(t1));  // open: clr
  Register #(.width(32)) register_26 (.D(R14IN), .en(RegWEn), .clk(clk), .Q(R14Out));  // open: clr
  Register #(.width(32)) register_27 (.D(R22IN), .en(RegWEn), .clk(clk), .Q(R22Out));  // open: clr
  Register #(.width(32)) register_28 (.D(R30IN), .en(RegWEn), .clk(clk), .Q(R30Out));  // open: clr
  Multiplexer #(.enable("false"), .select(5), .width(32)) multiplexer_2 (
    .in0(R0Out), .in1(ra), .in2(sp), .in3(R3Out), .in4(R4Out), .in5(t0), .in6(t1), .in7(t2), .in8(s0),
    .in9(s1), .in10(a0), .in11(R11Out), .in12(R12Out), .in13(R13Out), .in14(R14Out), .in15(R15Out),
    .in16(R16Out), .in17(R17Out), .in18(R18Out), .in19(R19Out), .in20(R20Out), .in21(R21Out), .in22(R22Out),
    .in23(R23Out), .in24(R24Out), .in25(R25Out), .in26(R26Out), .in27(R27Out), .in28(R28Out), .in29(R29Out),
    .in30(R30Out), .in31(R31Out), .out(Read_Data_1), .sel(rs1));
  Register #(.width(32)) register_29 (.D(R7IN), .en(RegWEn), .clk(clk), .Q(t2));  // open: clr
  Register #(.width(32)) register_30 (.D(R15IN), .en(RegWEn), .clk(clk), .Q(R15Out));  // open: clr
  Register #(.width(32)) register_31 (.D(R23IN), .en(RegWEn), .clk(clk), .Q(R23Out));  // open: clr
  Register #(.width(32)) register_32 (.D(R31IN), .en(RegWEn), .clk(clk), .Q(R31Out));  // open: clr
  Comparator #(.mode("unsigned"), .width(5)) comparator_1 (.a(rd), .b(5'b00001), .eq(comparator_1_eq));  // open: gt, lt
  Comparator #(.mode("unsigned"), .width(5)) comparator_2 (.a(rd), .b(5'b00010), .eq(comparator_2_eq));  // open: gt, lt
  Comparator #(.mode("unsigned"), .width(5)) comparator_3 (.a(rd), .b(5'b00011), .eq(comparator_3_eq));  // open: gt, lt
  Comparator #(.mode("unsigned"), .width(5)) comparator_4 (.a(rd), .b(5'b00100), .eq(comparator_4_eq));  // open: gt, lt
  Comparator #(.mode("unsigned"), .width(5)) comparator_5 (.a(rd), .b(5'b00101), .eq(comparator_5_eq));  // open: gt, lt
  Comparator #(.mode("unsigned"), .width(5)) comparator_6 (.a(rd), .b(5'b00110), .eq(comparator_6_eq));  // open: gt, lt
  Comparator #(.mode("unsigned"), .width(5)) comparator_7 (.a(rd), .b(5'b00111), .eq(comparator_7_eq));  // open: gt, lt
  Comparator #(.mode("unsigned"), .width(5)) comparator_8 (.a(rd), .b(5'b01000), .eq(comparator_8_eq));  // open: gt, lt
  Multiplexer #(.enable("false"), .width(32)) multiplexer_3 (
    .in0(ra), .in1(Write_Data), .out(R1IN), .sel(comparator_1_eq));
  Multiplexer #(.enable("false"), .width(32)) multiplexer_4 (
    .in0(sp), .in1(Write_Data), .out(R2IN), .sel(comparator_2_eq));
  Multiplexer #(.enable("false"), .width(32)) multiplexer_5 (
    .in0(R3Out), .in1(Write_Data), .out(R3IN), .sel(comparator_3_eq));
  Multiplexer #(.enable("false"), .width(32)) multiplexer_6 (
    .in0(R4Out), .in1(Write_Data), .out(R4IN), .sel(comparator_4_eq));
  Multiplexer #(.enable("false"), .width(32)) multiplexer_7 (
    .in0(t0), .in1(Write_Data), .out(R5IN), .sel(comparator_5_eq));
  Multiplexer #(.enable("false"), .width(32)) multiplexer_8 (
    .in0(t1), .in1(Write_Data), .out(R6IN), .sel(comparator_6_eq));
  Multiplexer #(.enable("false"), .width(32)) multiplexer_9 (
    .in0(t2), .in1(Write_Data), .out(R7IN), .sel(comparator_7_eq));
  Multiplexer #(.enable("false"), .width(32)) multiplexer_10 (
    .in0(s0), .in1(Write_Data), .out(R8IN), .sel(comparator_8_eq));
  Comparator #(.mode("unsigned"), .width(5)) comparator_9 (.a(rd), .b(5'b01001), .eq(comparator_9_eq));  // open: gt, lt
  Comparator #(.mode("unsigned"), .width(5)) comparator_10 (
    .a(rd), .b(5'b01010), .eq(comparator_10_eq));  // open: gt, lt
  Comparator #(.mode("unsigned"), .width(5)) comparator_11 (
    .a(rd), .b(5'b01011), .eq(comparator_11_eq));  // open: gt, lt
  Comparator #(.mode("unsigned"), .width(5)) comparator_12 (
    .a(rd), .b(5'b01100), .eq(comparator_12_eq));  // open: gt, lt
  Comparator #(.mode("unsigned"), .width(5)) comparator_13 (
    .a(rd), .b(5'b01101), .eq(comparator_13_eq));  // open: gt, lt
  Comparator #(.mode("unsigned"), .width(5)) comparator_14 (
    .a(rd), .b(5'b01110), .eq(comparator_14_eq));  // open: gt, lt
  Comparator #(.mode("unsigned"), .width(5)) comparator_15 (
    .a(rd), .b(5'b01111), .eq(comparator_15_eq));  // open: gt, lt
  Comparator #(.mode("unsigned"), .width(5)) comparator_16 (
    .a(rd), .b(5'b10000), .eq(comparator_16_eq));  // open: gt, lt
  Multiplexer #(.enable("false"), .width(32)) multiplexer_11 (
    .in0(s1), .in1(Write_Data), .out(R9IN), .sel(comparator_9_eq));
  Multiplexer #(.enable("false"), .width(32)) multiplexer_12 (
    .in0(a0), .in1(Write_Data), .out(R10IN), .sel(comparator_10_eq));
  Multiplexer #(.enable("false"), .width(32)) multiplexer_13 (
    .in0(R11Out), .in1(Write_Data), .out(R11IN), .sel(comparator_11_eq));
  Multiplexer #(.enable("false"), .width(32)) multiplexer_14 (
    .in0(R12Out), .in1(Write_Data), .out(R12IN), .sel(comparator_12_eq));
  Multiplexer #(.enable("false"), .width(32)) multiplexer_15 (
    .in0(R13Out), .in1(Write_Data), .out(R13IN), .sel(comparator_13_eq));
  Multiplexer #(.enable("false"), .width(32)) multiplexer_16 (
    .in0(R14Out), .in1(Write_Data), .out(R14IN), .sel(comparator_14_eq));
  Multiplexer #(.enable("false"), .width(32)) multiplexer_17 (
    .in0(R15Out), .in1(Write_Data), .out(R15IN), .sel(comparator_15_eq));
  Multiplexer #(.enable("false"), .width(32)) multiplexer_18 (
    .in0(R16Out), .in1(Write_Data), .out(R16IN), .sel(comparator_16_eq));
  Comparator #(.mode("unsigned"), .width(5)) comparator_17 (
    .a(rd), .b(5'b10001), .eq(comparator_17_eq));  // open: gt, lt
  Comparator #(.mode("unsigned"), .width(5)) comparator_18 (
    .a(rd), .b(5'b10010), .eq(comparator_18_eq));  // open: gt, lt
  Comparator #(.mode("unsigned"), .width(5)) comparator_19 (
    .a(rd), .b(5'b10011), .eq(comparator_19_eq));  // open: gt, lt
  Comparator #(.mode("unsigned"), .width(5)) comparator_20 (
    .a(rd), .b(5'b10100), .eq(comparator_20_eq));  // open: gt, lt
  Comparator #(.mode("unsigned"), .width(5)) comparator_21 (
    .a(rd), .b(5'b10101), .eq(comparator_21_eq));  // open: gt, lt
  Comparator #(.mode("unsigned"), .width(5)) comparator_22 (
    .a(rd), .b(5'b10110), .eq(comparator_22_eq));  // open: gt, lt
  Comparator #(.mode("unsigned"), .width(5)) comparator_23 (
    .a(rd), .b(5'b10111), .eq(comparator_23_eq));  // open: gt, lt
  Comparator #(.mode("unsigned"), .width(5)) comparator_24 (
    .a(rd), .b(5'b11000), .eq(comparator_24_eq));  // open: gt, lt
  Multiplexer #(.enable("false"), .width(32)) multiplexer_19 (
    .in0(R17Out), .in1(Write_Data), .out(R17IN), .sel(comparator_17_eq));
  Multiplexer #(.enable("false"), .width(32)) multiplexer_20 (
    .in0(R18Out), .in1(Write_Data), .out(R18IN), .sel(comparator_18_eq));
  Multiplexer #(.enable("false"), .width(32)) multiplexer_21 (
    .in0(R19Out), .in1(Write_Data), .out(R19IN), .sel(comparator_19_eq));
  Multiplexer #(.enable("false"), .width(32)) multiplexer_22 (
    .in0(R20Out), .in1(Write_Data), .out(R20IN), .sel(comparator_20_eq));
  Multiplexer #(.enable("false"), .width(32)) multiplexer_23 (
    .in0(R21Out), .in1(Write_Data), .out(R21IN), .sel(comparator_21_eq));
  Multiplexer #(.enable("false"), .width(32)) multiplexer_24 (
    .in0(R22Out), .in1(Write_Data), .out(R22IN), .sel(comparator_22_eq));
  Multiplexer #(.enable("false"), .width(32)) multiplexer_25 (
    .in0(R23Out), .in1(Write_Data), .out(R23IN), .sel(comparator_23_eq));
  Multiplexer #(.enable("false"), .width(32)) multiplexer_26 (
    .in0(R24Out), .in1(Write_Data), .out(R24IN), .sel(comparator_24_eq));
  Comparator #(.mode("unsigned"), .width(5)) comparator_25 (
    .a(rd), .b(5'b11001), .eq(comparator_25_eq));  // open: gt, lt
  Comparator #(.mode("unsigned"), .width(5)) comparator_26 (
    .a(rd), .b(5'b11010), .eq(comparator_26_eq));  // open: gt, lt
  Comparator #(.mode("unsigned"), .width(5)) comparator_27 (
    .a(rd), .b(5'b11011), .eq(comparator_27_eq));  // open: gt, lt
  Comparator #(.mode("unsigned"), .width(5)) comparator_28 (
    .a(rd), .b(5'b11100), .eq(comparator_28_eq));  // open: gt, lt
  Comparator #(.mode("unsigned"), .width(5)) comparator_29 (
    .a(rd), .b(5'b11101), .eq(comparator_29_eq));  // open: gt, lt
  Comparator #(.mode("unsigned"), .width(5)) comparator_30 (
    .a(rd), .b(5'b11110), .eq(comparator_30_eq));  // open: gt, lt
  Comparator #(.mode("unsigned"), .width(5)) comparator_31 (
    .a(rd), .b({5{1'b1}}), .eq(comparator_31_eq));  // open: gt, lt
  Multiplexer #(.enable("false"), .width(32)) multiplexer_27 (
    .in0(R25Out), .in1(Write_Data), .out(R25IN), .sel(comparator_25_eq));
  Multiplexer #(.enable("false"), .width(32)) multiplexer_28 (
    .in0(R26Out), .in1(Write_Data), .out(R26IN), .sel(comparator_26_eq));
  Multiplexer #(.enable("false"), .width(32)) multiplexer_29 (
    .in0(R27Out), .in1(Write_Data), .out(R27IN), .sel(comparator_27_eq));
  Multiplexer #(.enable("false"), .width(32)) multiplexer_30 (
    .in0(R28Out), .in1(Write_Data), .out(R28IN), .sel(comparator_28_eq));
  Multiplexer #(.enable("false"), .width(32)) multiplexer_31 (
    .in0(R29Out), .in1(Write_Data), .out(R29IN), .sel(comparator_29_eq));
  Multiplexer #(.enable("false"), .width(32)) multiplexer_32 (
    .in0(R30Out), .in1(Write_Data), .out(R30IN), .sel(comparator_30_eq));
  Multiplexer #(.enable("false"), .width(32)) multiplexer_33 (
    .in0(R31Out), .in1(Write_Data), .out(R31IN), .sel(comparator_31_eq));

  // Other names for the same wires on the sheet: R1Out[31:0] = ra; R2Out[31:0] = sp; R5Out[31:0] = t0;
  //   R6Out[31:0] = t1; R7Out[31:0] = t2; R8Out[31:0] = s0; R9Out[31:0] = s1; R10Out[31:0] = a0;
  //   read_data1[31:0] = Read_Data_1; read_data2[31:0] = Read_Data_2; read_reg1[4:0] = rs1; read_reg2[4:0] = rs2;
  //   write_en = RegWEn; write_reg[4:0] = rd

  // Notes on the sheet:
  //   INPUTS to your circuit
  //   DON'T CHANGE THE LOCATIONS OF THE INPUTS AND OUTPUTS!
  //   These are DEBUG/TEST outputs from your circuit.
  //   OUTPUTS from your circuit
endmodule
